// Logisim project 2 4 2 1 TO BCD.circ as structural Verilog: 1 circuit, main circuit main
module main (
  input  A,
  input  B,
  input  C,
  input  D,
  output W,
  output X,
  output Y,
  output Z
);

  wire and_1_out, and_2_out, not_1_out, not_2_out;

  not not_1 (not_1_out, B);
  and and_1 (and_1_out, B, not_2_out);
  not not_2 (not_2_out, C);
  xor xor_1 (Y, C, A);
  or or_1 (X, and_2_out, and_1_out);
  and and_2 (and_2_out, not_1_out, A);
  and and_3 (W, B, C);

  assign Z = D;

  // Notes on the sheet:
  //   2 4 2 1  TO  BCD
endmodule
