// Logisim project 2BITMULTIPLIER.circ as structural Verilog: 1 circuit, main circuit main
module main (
  input  A0,
  input  A1,
  input  B0,
  input  B1,
  output C0,
  output C1,
  output C2,
  output C3
);

  wire adder_2_cout, and_1_out, and_2_out, and_3_out;

  and and_1 (and_1_out, B1, A1);
  Adder #(.width(1)) adder_1 (.a(and_1_out), .b(adder_2_cout), .out(C2), .cout(C3));  // open: cin
  and and_2 (and_2_out, B0, A1);
  and and_3 (and_3_out, B1, A0);
  Adder #(.width(1)) adder_2 (.a(and_3_out), .b(and_2_out), .out(C1), .cout(adder_2_cout));  // open: cin
  and and_4 (C0, B0, A0);

  // Notes on the sheet:
  //   2 bit multiplier
endmodule
