// Logisim project 2wayswitch.circ as structural Verilog: 1 circuit, main circuit main
module main (
  input  switch1,
  input  in_2,
  input  switch1_2,
  input  switch2
);

  wire and_1_out, and_2_out, not_1_out, not_2_out, or_1_out, xnor_1_out;

  not not_1 (not_1_out, switch1);
  not not_2 (not_2_out, in_2);
  and and_1 (and_1_out, switch1, in_2);
  and and_2 (and_2_out, not_1_out, not_2_out);
  LED led_1 (.in(xnor_1_out));
  xnor xnor_1 (xnor_1_out, switch1_2, switch2);
  or or_1 (or_1_out, and_1_out, and_2_out);
  LED led_2 (.in(or_1_out));

  // Notes on the sheet:
  //                                                                2 way switch
  //   switch2
  //                       XNOR Gate
  //   LED
  //   LED
  //   xy+x'y'
  //   xy+x'y'
endmodule
