// Logisim project 3wayswitch.circ as structural Verilog: 1 circuit, main circuit main
module main (
  input  x,
  input  y,
  input  z
);

  wire and_1_out, and_2_out, and_3_out, and_4_out, not_1_out, not_2_out, not_3_out, or_1_out;

  not not_1 (not_1_out, y);
  not not_2 (not_2_out, x);
  not not_3 (not_3_out, z);
  and and_1 (and_1_out, x, y, z);
  and and_2 (and_2_out, x, not_1_out, not_3_out);
  and and_3 (and_3_out, not_2_out, y, not_3_out);
  and and_4 (and_4_out, not_2_out, not_1_out, z);
  or or_1 (or_1_out, and_1_out, and_2_out, and_3_out, and_4_out);
  LED led_1 (.in(or_1_out));

  // Notes on the sheet:
  //                                            3 way switch
  //                    xyz+xy'z'+x'yz'+x'y'z
  //      LED
endmodule
