// Logisim project 3x8usinggates.circ as structural Verilog: 1 circuit, main circuit main
module main (
  input  a,
  input  b,
  input  c,
  output out_4,
  output a_prime_b_prime_c,
  output a_prime_bc_prime,
  output a_prime_bc,
  output ab_prime_c_prime,
  output ab_prime_c,
  output abc_prime,
  output abc
);

  wire not_1_out, not_2_out, not_3_out;

  not not_1 (not_1_out, a);
  not not_2 (not_2_out, b);
  not not_3 (not_3_out, c);
  and and_1 (out_4, not_1_out, not_2_out, not_3_out);
  and and_2 (a_prime_b_prime_c, not_1_out, not_2_out, c);
  and and_3 (a_prime_bc_prime, not_1_out, b, not_3_out);
  and and_4 (a_prime_bc, not_1_out, b, c);
  and and_5 (ab_prime_c_prime, a, not_2_out, not_3_out);
  and and_6 (ab_prime_c, a, not_2_out, c);
  and and_7 (abc_prime, a, b, not_3_out);
  and and_8 (abc, b, a, c);

  // Notes on the sheet:
  //              a'b'c'
  //   3-8decoder
  //                                             nisarg parikh 150280107048
  //        jash khatri 150280107033
endmodule
