// Logisim project 8 4 -2 -1 T O BCD.circ as structural Verilog: 1 circuit, main circuit main
module main (
  input  A,
  input  B,
  input  C,
  input  D,
  output W,
  output X,
  output Y,
  output Z
);

  wire and_1_out, and_2_out, and_3_out, and_4_out, not_1_out, not_2_out, not_3_out, or_1_out;

  not not_1 (not_1_out, B);
  not not_2 (not_2_out, C);
  not not_3 (not_3_out, D);
  and and_1 (and_1_out, A, not_2_out, not_3_out);
  and and_2 (and_2_out, A, B);
  and and_3 (and_3_out, B, not_3_out, not_2_out);
  or or_1 (or_1_out, C, D);
  or or_2 (W, and_1_out, and_2_out);
  or or_3 (X, and_3_out, and_4_out);
  and and_4 (and_4_out, not_1_out, or_1_out);
  xor xor_1 (Y, C, D);

  assign Z = D;

  // Notes on the sheet:
  //   8 4 -2 -1  TO  BCD
endmodule
