// Logisim project ADD AND SUB.circ as structural Verilog: 1 circuit, main circuit main
module main (
  input  in_1,
  input  in_2,
  input  in_3,
  input  in_4,
  input  in_5,
  input  in_6,
  input  in_7,
  input  in_8,
  input  M,
  output out_10,
  output out_11,
  output out_12,
  output Z,
  output W
);

  wire adder_2_cout, adder_3_cout, adder_4_cout, xor_1_out, xor_2_out, xor_3_out, xor_4_out;

  xor xor_1 (xor_1_out, in_1, M);
  Adder #(.width(1)) adder_1 (.a(in_2), .b(xor_1_out), .out(out_10), .cin(adder_2_cout), .cout(W));
  xor xor_2 (xor_2_out, in_3, M);
  Adder #(.width(1)) adder_2 (.a(xor_2_out), .b(in_4), .out(out_11), .cin(adder_3_cout), .cout(adder_2_cout));
  xor xor_3 (xor_3_out, in_5, M);
  Adder #(.width(1)) adder_3 (.a(xor_3_out), .b(in_6), .out(out_12), .cin(adder_4_cout), .cout(adder_3_cout));
  xor xor_4 (xor_4_out, in_7, M);
  Adder #(.width(1)) adder_4 (.a(xor_4_out), .b(in_8), .out(Z), .cin(M), .cout(adder_4_cout));

  // Notes on the sheet:
  //   B3
  //   A3
  //   X
  //   B2
  //   A2
  //   Y
  //   B1
  //   A1
  //   Y
  //   A0
  //   B0
  //   KHATRI  JASH  150280107033
  //   MAHARSHI  NAYAK     150280107046
  //   NISARG  PARIKH   150280107048
endmodule
