// Logisim project BCDADDER.circ as structural Verilog: 1 circuit, main circuit main
module main (
  input  in_1,
  input  A0,
  input  B0,
  input  in_4,
  input  A1,
  input  B1,
  input  A2,
  input  B2,
  input  A3,
  input  B3,
  input  in_11,
  output Z,
  output Y,
  output X,
  output W,
  output V
);

  wire adder_1_cout, adder_1_out, adder_2_cout, adder_2_out, adder_3_cout, adder_3_out, adder_4_cout,
       adder_4_out, adder_5_cout, adder_6_cout, adder_7_cout, and_1_out, and_2_out, or_1_out;

  Adder #(.width(1)) adder_1 (.a(A0), .b(B0), .out(adder_1_out), .cout(adder_1_cout));  // open: cin
  Adder #(.width(1)) adder_2 (.a(A1), .b(B1), .out(adder_2_out), .cin(adder_1_cout), .cout(adder_2_cout));
  Adder #(.width(1)) adder_3 (.a(A2), .b(B2), .out(adder_3_out), .cin(adder_2_cout), .cout(adder_3_cout));
  Adder #(.width(1)) adder_4 (.a(A3), .b(B3), .out(adder_4_out), .cin(adder_3_cout), .cout(adder_4_cout));
  and and_1 (and_1_out, adder_4_out, adder_2_out);
  and and_2 (and_2_out, adder_4_out, adder_3_out);
  Adder #(.width(1)) adder_5 (.a(adder_1_out), .b(in_4), .out(Z), .cin(in_1), .cout(adder_5_cout));
  Adder #(.width(1)) adder_6 (.a(adder_2_out), .b(or_1_out), .out(Y), .cin(adder_5_cout), .cout(adder_6_cout));
  Adder #(.width(1)) adder_7 (.a(adder_3_out), .b(or_1_out), .out(X), .cin(adder_6_cout), .cout(adder_7_cout));
  Adder #(.width(1)) adder_8 (.a(adder_4_out), .b(in_11), .out(W), .cin(adder_7_cout), .cout(V));
  or or_1 (or_1_out, and_1_out, adder_4_cout, and_2_out);

  // Notes on the sheet:
  //   BCD ADDER
endmodule
