// Logisim project BINARY CONVERSION-2.circ as structural Verilog: 1 circuit, main circuit main
module main (
  input  A,
  input  B,
  input  C,
  input  D,
  output W,
  output X,
  output Y,
  output Z
);

  or or_1 (X, A, B);
  xor xor_1 (Z, C, D);
  xor xor_2 (Y, B, C);

  assign W = A;

  // Notes on the sheet:
  //                                                        BINARY TO GRAY CODE
  //                                                                   BINARY- EXCESS 3 CODE
  //                                                     PATEL DARSHIT       150280107061
  //                                                                  PATEL TAPAN       150280107080
  //                                                          PATEL KASHYAP         150280107069
  //                                 BINARY TO 84(-2)(-1) CODE
endmodule
