// Logisim project BINTOGRAY.circ as structural Verilog: 1 circuit, main circuit main
module main (
  input  A,
  input  B,
  input  C,
  input  D,
  output W_AB_prime_C_prime,
  output X_A_prime_B_A_prime_B_prime_C_prime,
  output out_7,
  output out_8
);

  wire and_2_out, and_3_out, and_4_out, and_5_out, and_6_out, and_7_out, and_8_out, and_9_out, not_1_out,
       not_2_out, not_3_out, not_4_out, or_1_out, xor_1_out;

  not not_1 (not_1_out, A);
  not not_2 (not_2_out, B);
  not not_3 (not_3_out, C);
  not not_4 (not_4_out, D);
  xor xor_1 (xor_1_out, A, D);
  and and_1 (W_AB_prime_C_prime, A, not_2_out, not_3_out);
  and and_2 (and_2_out, not_1_out, B);
  and and_3 (and_3_out, A, not_2_out, not_3_out);
  or or_1 (or_1_out, not_4_out, B);
  or or_2 (X_A_prime_B_A_prime_B_prime_C_prime, and_2_out, and_3_out);
  and and_4 (and_4_out, not_1_out, not_2_out, C);
  and and_5 (and_5_out, not_1_out, C, D);
  and and_6 (and_6_out, not_2_out, not_3_out, xor_1_out);
  and and_7 (and_7_out, C, not_1_out, or_1_out);
  and and_8 (and_8_out, A, not_2_out, not_3_out);
  and and_9 (and_9_out, B, not_1_out, not_3_out, not_4_out);
  or or_3 (out_8, and_6_out, and_7_out);
  or or_4 (out_7, and_9_out, and_8_out, and_4_out, and_5_out);

  // Notes on the sheet:
  //   NISARG PARIKH-150280107048
  //   KHATRI JASH-150280107033
  //                                               Y=A'BC'D'+AB'C+A'CD+A'B'C
  //   Z=A'C(B+D')+B'C'(A'D+AD')
endmodule
