// Logisim project BINTOX3.circ as structural Verilog: 1 circuit, main circuit main
module main (
  input  A,
  input  B,
  input  C,
  input  D,
  output W__A_B_C_D,
  output out_6,
  output out_7,
  output Z_D_prime
);

  wire and_1_out, and_2_out, and_3_out, not_1_out, not_3_out, or_1_out;

  not not_1 (not_1_out, C);
  or or_1 (or_1_out, C, D);
  not not_2 (Z_D_prime, D);
  and and_1 (and_1_out, B, or_1_out);
  or or_2 (W__A_B_C_D, A, and_1_out);
  not not_3 (not_3_out, B);
  xnor xnor_1 (out_7, C, D);
  and and_2 (and_2_out, B, not_1_out, Z_D_prime);
  and and_3 (and_3_out, not_3_out, or_1_out);
  or or_3 (out_6, and_2_out, and_3_out);

  // Notes on the sheet:
  //                X=B'(C+D')+BC'D'
  //               Y=C'D'+CD
  //   KHATRI JASH 150280107033
  //   NISARG PARIKH-150280107048
endmodule
