// Logisim project GREY TO BCD.circ as structural Verilog: 1 circuit, main circuit main
module main (
  input  A,
  input  B,
  input  C,
  input  D,
  output V,
  output W,
  output X,
  output Y,
  output Z
);

  wire and_1_out, and_2_out, and_3_out, and_4_out, and_5_out, and_6_out, and_7_out, and_8_out, and_10_out,
       and_11_out, not_1_out, not_2_out, not_3_out, xnor_1_out, xor_1_out;

  not not_1 (not_1_out, A);
  not not_2 (not_2_out, B);
  xor xor_1 (xor_1_out, C, D);
  not not_3 (not_3_out, C);
  xnor xnor_1 (xnor_1_out, C, D);
  and and_1 (and_1_out, xnor_1_out, not_1_out, B);
  and and_2 (and_2_out, not_1_out, not_2_out, xor_1_out);
  and and_3 (and_3_out, xor_1_out, B, A);
  and and_4 (and_4_out, A, not_2_out, xnor_1_out);
  and and_5 (and_5_out, not_1_out, B, not_3_out);
  or or_1 (Y, and_5_out, and_6_out);
  and and_6 (and_6_out, not_2_out, C);
  and and_7 (and_7_out, not_1_out, B);
  or or_2 (X, and_7_out, and_8_out);
  and and_8 (and_8_out, not_2_out, not_3_out, A);
  or or_3 (Z, and_4_out, and_1_out, and_2_out, and_3_out);
  and and_9 (W, A, B, not_3_out);
  and and_10 (and_10_out, A, C);
  and and_11 (and_11_out, A, not_2_out);
  or or_4 (V, and_10_out, and_11_out);

  // Notes on the sheet:
  //                 GREY CODE  TO  BCD 
endmodule
