// Logisim project SRFF.circ as structural Verilog: 1 circuit, main circuit main
module main (
  input  R,
  input  S,
  input  S_2,
  input  R_2,
  input  S_3,
  input  En,
  input  R_3,
  output Q,
  output Q_2,
  output Q_prime,
  output Q_prime_2,
  output Q_3,
  output Q_prime_3
);

  wire nand_1_out, nand_2_out;

  nor nor_1 (Q, R, Q_prime);
  nor nor_2 (Q_prime, Q, S_2);
  nand nand_1 (nand_1_out, S_3, En);
  nand nand_2 (nand_2_out, En, R_3);
  nand nand_3 (Q_3, nand_1_out, Q_prime_3);
  nand nand_4 (Q_prime_3, Q_3, nand_2_out);
  nand nand_5 (Q_2, S, Q_prime_2);
  nand nand_6 (Q_prime_2, Q_2, R_2);

  // Notes on the sheet:
  //   S-R Flip Flops
endmodule
