// Logisim project X3 TO BCD.circ as structural Verilog: 1 circuit, main circuit main
module main (
  input  A,
  input  B,
  input  C,
  input  D,
  output W,
  output X,
  output Y,
  output Z
);

  wire and_1_out, and_2_out, and_3_out, and_4_out, and_5_out, not_1_out, not_2_out;

  not not_1 (not_1_out, B);
  not not_2 (not_2_out, C);
  and and_1 (and_1_out, A, B);
  and and_2 (and_2_out, A, C, D);
  and and_3 (and_3_out, B, D, C);
  and and_4 (and_4_out, not_1_out, not_2_out);
  not not_3 (Z, D);
  or or_1 (W, and_1_out, and_2_out);
  or or_2 (X, and_3_out, and_4_out, and_5_out);
  and and_5 (and_5_out, not_1_out, Z);
  xor xor_1 (Y, C, D);

  // Notes on the sheet:
  //                     EXCESS 3 CODE  TO   BCD
endmodule
