// Logisim project adder.circ as structural Verilog: 1 circuit, main circuit main
module main (
  input  a,
  input  b,
  input  in_3,
  output out_4,
  output out_5
);

  wire and_1_out, and_2_out, xor_1_out;

  xor xor_1 (xor_1_out, a, b);
  and and_1 (and_1_out, b, a);
  xor xor_2 (out_4, xor_1_out, in_3);
  and and_2 (and_2_out, xor_1_out, in_3);
  or or_1 (out_5, and_1_out, and_2_out);

  // Notes on the sheet:
  //   NISARG PARIKH 150280107048
  //    inital carry 
  //   FULL ADDER
  //   sum
  //   carry
endmodule
