// Logisim project carrylookahead.circ as structural Verilog: 1 circuit, main circuit main
module main (
  input  b4,
  input  a4,
  input  b3,
  input  a3,
  input  b2,
  input  a2,
  input  b1,
  input  a1,
  input  c1,
  output out_10,
  output out_11,
  output out_12,
  output out_13,
  output out_14
);

  wire and_1_out, and_2_out, and_3_out, and_4_out, and_5_out, and_6_out, and_7_out, and_8_out, and_9_out,
       and_10_out, and_11_out, and_12_out, and_13_out, and_14_out, or_2_out, or_3_out, or_4_out, xor_1_out,
       xor_2_out, xor_3_out, xor_4_out;

  xor xor_1 (xor_1_out, b4, a4);
  and and_1 (and_1_out, b4, a4);
  xor xor_2 (xor_2_out, b3, a3);
  and and_2 (and_2_out, b3, a3);
  xor xor_3 (xor_3_out, b2, a2);
  and and_3 (and_3_out, b2, a2);
  xor xor_4 (xor_4_out, b1, a1);
  and and_4 (and_4_out, b1, a1);
  and and_5 (and_5_out, c1, xor_4_out, xor_3_out, xor_2_out, xor_1_out);
  and and_6 (and_6_out, xor_1_out, xor_2_out, xor_3_out, and_4_out);
  and and_7 (and_7_out, xor_1_out, xor_2_out, and_3_out);
  and and_8 (and_8_out, xor_1_out, and_2_out);
  and and_9 (and_9_out, xor_2_out, xor_3_out, xor_4_out, c1);
  and and_10 (and_10_out, xor_2_out, xor_3_out, and_4_out);
  and and_11 (and_11_out, xor_2_out, and_3_out);
  and and_12 (and_12_out, xor_3_out, xor_4_out, c1);
  and and_13 (and_13_out, xor_3_out, and_4_out);
  and and_14 (and_14_out, xor_4_out, c1);
  or or_1 (out_10, and_1_out, and_5_out, and_6_out, and_7_out, and_8_out);
  or or_2 (or_2_out, and_9_out, and_2_out, and_2_out, and_11_out);
  or or_3 (or_3_out, and_3_out, and_12_out, and_13_out);
  or or_4 (or_4_out, and_4_out, and_14_out);
  xor xor_5 (out_11, xor_1_out, or_2_out);
  or or_5 (out_12, and_10_out, or_3_out);
  xor xor_6 (out_13, xor_3_out, or_4_out);
  xor xor_7 (out_14, xor_4_out, c1);

  // Notes on the sheet:
  //                                                          LOOK AHEAD CARRY GENERATOR
  //   p4
  //   g4
  //   p3
  //   g3
  //   p2
  //   g2
  //   p1
  //   g1
  //   c1
  //   c5
  //   c4
  //   c3
  //   c2
endmodule
