// Logisim project counter.circ as structural Verilog: 1 circuit, main circuit main
module main (
  input  in_1,
  input  in_2,
  input  in_3,
  input  in_4,
  input  in_5,
  input  in_6,
  input  in_7,
  input  in_8,
  output out_9,
  output out_10,
  output out_11,
  output out_12
);

  wire clock_1_out;

  Clock clock_1 (.out(clock_1_out));
  J_K_Flip_Flop j_k_ff_1 (.J(in_1), .clk(clock_1_out), .K(in_5), .Q(out_9));  // open: Qn, preset, en, reset
  J_K_Flip_Flop j_k_ff_2 (.J(in_2), .clk(out_9), .K(in_6), .Q(out_10));  // open: Qn, preset, en, reset
  J_K_Flip_Flop j_k_ff_3 (.J(in_3), .clk(out_10), .K(in_7), .Q(out_11));  // open: Qn, preset, en, reset
  J_K_Flip_Flop j_k_ff_4 (.J(in_4), .clk(out_11), .K(in_8), .Q(out_12));  // open: Qn, preset, en, reset
endmodule
