// Logisim project decrementorFA.circ as structural Verilog: 1 circuit, main circuit main
module main (
  input  in_1,
  input  A0,
  input  A1,
  input  A2,
  input  A3,
  output B0,
  output B1,
  output B2,
  output B3
);

  wire adder_1_cout, adder_2_cout, adder_3_cout;

  Adder #(.width(1)) adder_1 (.a(A0), .b(in_1), .out(B0), .cout(adder_1_cout));  // open: cin
  Adder #(.width(1)) adder_2 (.a(A1), .b(in_1), .out(B1), .cin(adder_1_cout), .cout(adder_2_cout));
  Adder #(.width(1)) adder_3 (.a(A2), .b(in_1), .out(B2), .cin(adder_2_cout), .cout(adder_3_cout));
  Adder #(.width(1)) adder_4 (.a(A3), .b(in_1), .out(B3), .cin(adder_3_cout));  // open: cout

  // Notes on the sheet:
  //   Decrementor circuit
endmodule
