// Logisim project fullsubtractor.circ as structural Verilog: 1 circuit, main circuit main
module main (
  input  X,
  input  B_in,
  input  Y,
  input  x_2,
  input  y_2,
  input  B_in_2,
  output D,
  output D_2,
  output B_out,
  output FS
);

  wire subtractor_2_bout, subtractor_2_out, subtractor_3_bout;

  Subtractor #(.width(1)) subtractor_1 (.a(x_2), .b(y_2), .out(D_2), .bin(B_in), .bout(FS));
  Subtractor #(.width(1)) subtractor_2 (.a(X), .b(Y), .out(subtractor_2_out), .bout(subtractor_2_bout));  // open: bin
  Subtractor #(.width(1)) subtractor_3 (
    .a(subtractor_2_out), .b(B_in_2), .out(D), .bout(subtractor_3_bout));  // open: bin
  or or_1 (B_out, subtractor_3_bout, subtractor_2_bout);

  // Notes on the sheet:
  //   B out
  //   Full Subtractor
  //   HS
  //   HS
endmodule
