// Logisim project half adder.circ as structural Verilog: 1 circuit, main circuit main
module main (
  input  a0,
  input  b0,
  output sum,
  output carry
);

  xor xor_1 (sum, a0, b0);
  and and_1 (carry, b0, a0);

  // Notes on the sheet:
  //   half  adder
endmodule
