// Logisim project half subtractor.circ as structural Verilog: 1 circuit, main circuit main
module main (
  input  a0,
  input  b0,
  output out_3,
  output out_4
);

  wire not_1_out;

  not not_1 (not_1_out, a0);
  xor xor_1 (out_3, a0, b0);
  and and_1 (out_4, b0, not_1_out);

  // Notes on the sheet:
  //   half  subtractor
  //                  difference
  //                borrow
endmodule
