// Logisim project incrementFA.circ as structural Verilog: 1 circuit, main circuit main
module main (
  input  A3,
  input  A2,
  input  A1,
  input  A0,
  output out_5,
  output B3,
  output B2,
  output B1,
  output B0
);

  wire adder_2_cout, adder_3_cout, adder_4_cout;

  Adder #(.width(1)) adder_1 (.a(A3), .b(adder_2_cout), .out(B3), .cin(1'b0), .cout(out_5));
  Adder #(.width(1)) adder_2 (.a(A2), .b(adder_4_cout), .out(B2), .cin(1'b0), .cout(adder_2_cout));
  Adder #(.width(1)) adder_3 (.a(A0), .b(1'b1), .out(B0), .cin(1'b0), .cout(adder_3_cout));
  Adder #(.width(1)) adder_4 (.a(A1), .b(adder_3_cout), .out(B1), .cin(1'b0), .cout(adder_4_cout));

  // Notes on the sheet:
  //                                                           Incrementor Circuit using FA
  //   C
endmodule
