// Logisim project voting.circ as structural Verilog: 1 circuit, main circuit main
module main (
  input  x,
  input  y,
  input  z,
  output vote
);

  wire and_1_out, and_2_out, and_3_out;

  and and_1 (and_1_out, x, y);
  and and_2 (and_2_out, y, z);
  and and_3 (and_3_out, x, z);
  or or_1 (vote, and_1_out, and_2_out, and_3_out);

  // Notes on the sheet:
  //                                                                                                             use: Majority wins voting
endmodule
